// Logisim project Template.circ as structural Verilog: 2 circuits, main circuit main
module main (
  input  in_1,
  output [14:0] out_2
);

  wire clk;

  // Text text_1: pin names not known
  // Text text_2: pin names not known
  // Text text_3: pin names not known
  // Text text_4: pin names not known
  // Text text_5: pin names not known
  Clock #(.highDuration(4), .lowDuration(4)) u_clk (.out(clk));
  Clock sysclk ();  // open: out
  PCINC_16BITS pcinc_16bits_1 (.clk(clk), .CLR(in_1), .FETCH_OUT(out_2));

  // Notes on the sheet:
  //   LABO ARO 2 - FETCH
  //   HEIG-VD / Institut REDS
  //   Date : 25.02.2014
  //   Ne pas modifier les noms des clocks
endmodule

module PCINC_16BITS (
  input  clk,
  input  CLR,
  output [14:0] FETCH_OUT
);

  wire [0:0] PC_q;
  wire [14:0] PC_q_2;
  wire [15:0] adder_1_out;

  // Text text_1: pin names not known
  // Text text_2: pin names not known
  // Text text_3: pin names not known
  // Text text_4: pin names not known
  // Text text_5: pin names not known
  Adder #(.width(16)) adder_1 (.a({PC_q_2, PC_q[0]}), .b(16'h2), .out(adder_1_out));  // open: cin, cout
  Register #(.width(16)) PC (.D(adder_1_out), .en(1'b1), .clk(clk), .Q({PC_q_2, PC_q[0]}), .clr(CLR));
  ROM #(.addrWidth(15), .dataWidth(15)) MEM_INSTRU (.addr(PC_q_2), .data(FETCH_OUT));

  // Notes on the sheet:
  //   contents of MEM_INSTRU (hex, n*v repeats v):
  //   2103 188b 18cc 2502
endmodule
